# Fritzing sketch canbus_example (saved by Fritzing 0.9.3b)
breadboards: 1

parts:
  Raspberry_Pi_1 = Raspberry Pi 3 [part_number=RPI-3-V1.2]
  Part1 = Arduino Uno (Rev3) - ICSP
  M1 = JoyIt can bus module [package=THT]
  M2 = JoyIt can bus module [package=THT]
  RE1 = Rotary Encoder [package=THT]
  J1 = Basic Servo

nets:
  N1: Raspberry_Pi_1.3v3, M1.pin1
  N2: Raspberry_Pi_1.GIPO10, M1.pin5
  N3: Raspberry_Pi_1.GIPO9, M1.pin4
  N4: Raspberry_Pi_1.GIPO11, M1.pin6
  N5: Raspberry_Pi_1.GIPO8, M1.pin3
  N6: Raspberry_Pi_1.GIPO25, M1.pin7
  N7: Raspberry_Pi_1.GND, M1.pin2
  N8: Raspberry_Pi_1.5V, M1.pin_14
  N9: Part1.A0, RE1.EncoderPinC
  N10: Part1.ICSP_MISO, Part1.D12/MISO, M2.pin4
  5V: Part1.5V, M2.pin_14, RE1.EncoderPinA, J1.vcc
  N11: Part1.D9_PWM, J1.pulse
  N12: Part1.D10_PWM/SS, M2.pin3
  N13: Part1.D11_PWM/MOSI, M2.pin5
  N14: Part1.D13/SCK, M2.pin6
  GND: Part1.GND, M2.pin2, RE1.EncoderPinB, J1.gnd
  N15: Part1.3V3, M2.pin1
  N16: M1.pin10, M1.pin12, M2.pin10
  N17: M1.pin11, M1.pin13, M2.pin11

notes:
  CANBUS
