# Fritzing sketch wiring_smarterdam_voertuig (saved by Fritzing 0.9.3b)

parts:
  Savox_SV-0236MG_Rechts = Basic Servo
  12V_Accu = Power plug
  Savox_SV-0236MG_Links = Basic Servo
  12V_to_7_4V_stepdown = DC_DC_XL4016 [package=board_screw]
  Raspberry_Pi1 = Raspberry Pi B+
  Motor_RRight = DC Motor with 3-phase hall-encoder [part_number=VT-E-G25A-06-177E]
  12V_killswitch = SWITCH-SPST-2 [package=switch-spst-vertical]
  12V_to_5V_stepdown = DC_DC_XL4016 [package=board_screw]
  To_RasPi_Power_(USB) = USB Connectors [package=usb-a-s]
  X2 = USB Connectors [package=usb-a-s]
  X3 = USB Connectors [package=usb-a-s]
  Part1 = SO-24x [chip_label=SO-24x package=SO(x)]  # not connected
  Motor_Controller_2 = IC, DIP package, 16 pins [chip_label="MC 2"]
  6X_10A_fuse_box = IC, DIP package, 8 pins [chip_label=IC]
  Display_Rechts = Nokia 6100 Color LCD [package=nokia6100_lcd]
  Motor_Controller_1 = IC, DIP package, 16 pins [chip_label="MC 1"]
  Motor_RLeft = DC Motor with 3-phase hall-encoder [part_number=VT-E-G25A-06-177E]
  8_Channel_Relay1 = 8 Channel Power Relay
  48V_Accu = Power plug
  48V_killswitch = SWITCH-SPST-2 [package=switch-spst-vertical]
  30A = FUSE [package=fuse_5mm]
  JP6 = Header 2 [package=molex-1x2_lock]
  JP7 = Header 2 [package=molex-1x2_lock]
  SB = Header 2 [package=molex-1x2_lock]
  JP9 = Header 3 [package=molex-1x3_lock]
  SG2 = Header 2 [package=molex-1x2_lock]
  SG1 = Header 2 [package=molex-1x2_lock]
  S1 = Toggle Switch [package=THT]
  12V_Oplader = Power plug
  S2 = Toggle Switch [package=THT]
  48V_Oplader = Power plug
  JP12 = Header 2 [package=molex-1x2_lock]
  JP13 = Header 2 [package=molex-1x2_lock]
  JP14 = Header 2 [package=molex-1x2_lock]
  Display_Links = Nokia 6100 Color LCD [package=nokia6100_lcd]
  JP15 = Header 2 [package=molex-1x2_lock]
  JP16 = Header 2 [package=molex-1x2_lock]  # not connected
  IC1 = IC, SIP package, 10 pins [chip_label="Common Ground"]
  JP17 = Header 2 [package=molex-1x2_lock]
  JP18 = Header 2 [package=molex-1x2_lock]

nets:
  GND: Savox_SV-0236MG_Rechts.gnd, Savox_SV-0236MG_Links.gnd, 12V_to_7_4V_stepdown.OUT-, Raspberry_Pi1.GND
  VCC: Savox_SV-0236MG_Rechts.vcc, Savox_SV-0236MG_Links.vcc, 12V_to_7_4V_stepdown.OUT+
  N1: Savox_SV-0236MG_Rechts.pulse, Raspberry_Pi1.GPIO3
  VCC_2: 12V_Accu.VCC, 12V_killswitch.O, 12V_Oplader.VCC
  N2: 12V_Accu.GND, S1.COM
  N3: Savox_SV-0236MG_Links.pulse, Raspberry_Pi1.GPIO2
  N4: 12V_to_7_4V_stepdown.IN+, 12V_killswitch.P, 12V_to_5V_stepdown.IN+
  N5: 12V_to_7_4V_stepdown.IN-, JP9.2
  N6: Raspberry_Pi1.GPIO27, SB.1
  N7: Raspberry_Pi1.GPIO21, JP17.2
  N8: Raspberry_Pi1.GPIO20, JP18.2
  N9: Raspberry_Pi1.GPIO12, JP15.2
  N10: Raspberry_Pi1.GPIO18, IC1.pin7
  5V: Raspberry_Pi1.5V, 8_Channel_Relay1.VCC
  N11: Motor_RRight.5V, Motor_Controller_2.pin1
  N12: Motor_RRight.5V_GND, Motor_Controller_2.pin2
  N13: Motor_RRight.HY, 8_Channel_Relay1.NO#35, 8_Channel_Relay1.NC#36
  N14: Motor_RRight.HG, 8_Channel_Relay1.NC#33, 8_Channel_Relay1.NO#38
  N15: Motor_RRight.HB, Motor_Controller_2.pin6
  N16: Motor_RRight.PY, 8_Channel_Relay1.NO#41, 8_Channel_Relay1.NC#42
  N17: Motor_RRight.PG, 8_Channel_Relay1.NC#39, 8_Channel_Relay1.NO#44
  N18: Motor_RRight.PB, Motor_Controller_2.pin3
  N19: 12V_to_5V_stepdown.IN-, JP9.1
  N20: 12V_to_5V_stepdown.OUT+, 6X_10A_fuse_box.pin8
  GND_2: 12V_to_5V_stepdown.OUT-, To_RasPi_Power_(USB).GND, X2.GND, X3.GND
  N21: To_RasPi_Power_(USB).VBUS, 6X_10A_fuse_box.pin4
  N22: X2.VBUS, 6X_10A_fuse_box.pin3
  N23: X3.VBUS, 6X_10A_fuse_box.pin2
  N24: Motor_Controller_2.pin4, 8_Channel_Relay1.COM#43
  N25: Motor_Controller_2.pin5, 8_Channel_Relay1.COM#40
  N26: Motor_Controller_2.pin7, 8_Channel_Relay1.COM#34
  N27: Motor_Controller_2.pin8, 8_Channel_Relay1.COM#37
  N28: Motor_Controller_2.pin10, IC1.pin6
  N29: Motor_Controller_2.pin11, IC1.pin1
  N30: Motor_Controller_2.pin12, Display_Rechts.DIO
  N31: Motor_Controller_2.pin13, Motor_Controller_1.pin13, SB.2
  N32: Motor_Controller_2.pin14, SG2.2
  N33: Motor_Controller_2.pin15, JP7.2
  N34: Motor_Controller_2.pin16, JP14.1
  N35: Motor_Controller_1.pin1, Motor_RLeft.5V
  N36: Motor_Controller_1.pin2, Motor_RLeft.5V_GND
  N37: Motor_Controller_1.pin3, Motor_RLeft.PB
  N38: Motor_Controller_1.pin4, 8_Channel_Relay1.COM#25
  N39: Motor_Controller_1.pin5, 8_Channel_Relay1.COM#22
  N40: Motor_Controller_1.pin6, Motor_RLeft.HB
  N41: Motor_Controller_1.pin7, 8_Channel_Relay1.COM#28
  N42: Motor_Controller_1.pin8, 8_Channel_Relay1.COM#31
  N43: Motor_Controller_1.pin10, IC1.pin4
  N44: Motor_Controller_1.pin11, IC1.pin3
  N45: Motor_Controller_1.pin12, Display_Links.SCK
  N46: Motor_Controller_1.pin14, SG1.2
  N47: Motor_Controller_1.pin15, JP6.1
  N48: Motor_Controller_1.pin16, JP13.1
  N49: Motor_RLeft.HY, 8_Channel_Relay1.NC#27, 8_Channel_Relay1.NO#32
  N50: Motor_RLeft.HG, 8_Channel_Relay1.NO#29, 8_Channel_Relay1.NC#30
  N51: Motor_RLeft.PY, 8_Channel_Relay1.NC#21, 8_Channel_Relay1.NO#26
  N52: Motor_RLeft.PG, 8_Channel_Relay1.NO#23, 8_Channel_Relay1.NC#24
  N53: 8_Channel_Relay1.GND, IC1.pin5
  N54: 8_Channel_Relay1.IN1, 8_Channel_Relay1.IN2, 8_Channel_Relay1.IN3, 8_Channel_Relay1.IN4, 8_Channel_Relay1.IN5, 8_Channel_Relay1.IN6, 8_Channel_Relay1.IN7, 8_Channel_Relay1.IN8, JP15.1
  VCC_3: 48V_Accu.VCC, 48V_killswitch.P, 48V_Oplader.VCC
  N55: 48V_Accu.GND, S2.COM
  N56: 48V_killswitch.O, 30A.2
  N57: 30A.1, JP12.1
  N58: JP6.2, JP7.1, S2.L1
  N59: JP9.3, S1.L1
  N60: SG2.1, JP18.1
  N61: SG1.1, JP17.1
  N62: S1.L2, 12V_Oplader.GND
  N63: S2.L2, 48V_Oplader.GND
  N64: JP12.2, JP13.2, JP14.2

notes:
  Bedrading moet nog doorgemeten worden op juiste kleur en positie
  48V
  Niet daadwerkelijke display, slechts een voorbeeld
  Dit component stelt een stekker/verbinding voor, waar twee draden van dezelfde kleur bij elkaar komen

custom parts:
  DC Motor with 3-phase hall-encoder: DC Motor with 3-phase and hall sensors
  8 Channel Power Relay: An 8 channel power relay. The module operates at 5V.
